// Logisim project project2_1.circ as structural Verilog: 2 circuits, main circuit main
module main (
);

  wire and_1_out, and_2_out, and_3_out, and_4_out, and_5_out, and_6_out, clock_1_out, clock_2_out, d_ff_1_qn,
       decoder_1_out0, decoder_1_out1, decoder_1_out2, decoder_1_out3, not_1_out, not_2_out, not_3_out,
       not_4_out, not_5_out, nums_1_a, nums_1_c, nums_1_d, nums_1_e, nums_1_f, nums_1_g, nums_1_out_6;
  wire [7:0] adder_1_out, adder_2_out, multiplexer_1_out, multiplexer_2_out, multiplexer_3_out,
       multiplexer_4_out, ram_1_dout, ram_2_dout, register_1_q, subtractor_1_out, X0_q, X1_q, X2_q, X3_q;

  Decoder #(.select(2)) decoder_1 (
    .out0(decoder_1_out0), .out1(decoder_1_out1), .out2(decoder_1_out2), .out3(decoder_1_out3),
    .sel(ram_2_dout[5:4]), .en(1'b1));
  Clock clock_1 (.out(clock_1_out));
  RAM ram_1 (.addr(multiplexer_3_out), .we(1'b0), .oe(1'b1), .clk(clock_1_out), .dout(ram_1_dout));  // open: din
  Clock #(.highDuration(2), .lowDuration(2)) clock_2 (.out(clock_2_out));
  Adder adder_1 (.a(multiplexer_3_out), .b(multiplexer_4_out), .out(adder_1_out));  // open: cin, cout
  Adder adder_2 (.a(register_1_q), .b(8'h1), .out(adder_2_out));  // open: cin, cout
  Register register_1 (.D(adder_2_out), .clk(clock_2_out), .Q(register_1_q));  // open: en, clr
  and and_1 (and_1_out, 1'b1, decoder_1_out0);
  and and_2 (and_2_out, 1'b1, decoder_1_out1);
  and and_3 (and_3_out, 1'b1, decoder_1_out2);
  and and_4 (and_4_out, 1'b1, decoder_1_out3);
  D_Flip_Flop d_ff_1 (.D(1'b1), .clk(clock_2_out), .Qn(d_ff_1_qn));  // open: Q, preset, reset
  Register X0 (.D(multiplexer_2_out), .en(and_1_out), .clk(clock_2_out), .Q(X0_q), .clr(d_ff_1_qn));
  Register X1 (.D(multiplexer_2_out), .en(and_2_out), .clk(clock_2_out), .Q(X1_q), .clr(d_ff_1_qn));
  Register X2 (.D(multiplexer_2_out), .en(and_3_out), .clk(clock_2_out), .Q(X2_q), .clr(d_ff_1_qn));
  Register X3 (.D(multiplexer_2_out), .en(and_4_out), .clk(clock_2_out), .Q(X3_q), .clr(d_ff_1_qn));
  Multiplexer #(.width(8)) multiplexer_1 (
    .in0(adder_1_out), .in1(subtractor_1_out), .out(multiplexer_1_out), .sel(ram_2_dout[6]));
  Multiplexer #(.width(8)) multiplexer_2 (
    .in0(multiplexer_1_out), .in1(ram_1_dout), .out(multiplexer_2_out), .sel(ram_2_dout[7]));
  RAM ram_2 (.addr(register_1_q), .we(1'b0), .oe(1'b1), .clk(clock_2_out), .dout(ram_2_dout));  // open: din
  Subtractor subtractor_1 (.a(multiplexer_3_out), .b(multiplexer_4_out), .out(subtractor_1_out));  // open: bin, bout
  Multiplexer #(.select(2), .width(8)) multiplexer_3 (
    .in0(X0_q), .in1(X1_q), .in2(X2_q), .in3(X3_q), .out(multiplexer_3_out), .sel(ram_2_dout[3:2]));
  Multiplexer #(.select(2), .width(8)) multiplexer_4 (
    .in0(X0_q), .in1(X1_q), .in2(X2_q), .in3(X3_q), .out(multiplexer_4_out), .sel(ram_2_dout[1:0]));
  not not_1 (not_1_out, ram_2_dout[6]);
  not not_2 (not_2_out, ram_2_dout[7]);
  not not_3 (not_3_out, ram_2_dout[6]);
  nums nums_1 (
    .in_1(1'b0), .in_2(1'b0), .B(ram_2_dout[5]), .in_4(ram_2_dout[4]), .a(nums_1_a), .out_6(nums_1_out_6),
    .c(nums_1_c), .d(nums_1_d), .e(nums_1_e), .f(nums_1_f), .g(nums_1_g));
  not not_4 (not_4_out, ram_2_dout[7]);
  not not_5 (not_5_out, ram_2_dout[7]);
  _7_Segment_Display u_7_segment_display_1 (
    .g(nums_1_g), .f(nums_1_f), .a(nums_1_a), .b(nums_1_out_6), .e(nums_1_e), .d(nums_1_d), .c(nums_1_c));  // open: dp
  and and_5 (and_5_out, not_1_out, not_4_out);
  LED led_1 (.in(not_2_out));
  LED led_2 (.in(not_2_out));
  LED led_3 (.in(not_2_out));
  LED led_4 (.in(not_2_out));
  LED led_5 (.in(not_2_out));
  LED led_6 (.in(not_2_out));
  and and_6 (and_6_out, not_5_out, not_3_out);
  LED led_7 (.in(and_5_out));
  LED led_8 (.in(and_5_out));
  LED led_9 (.in(and_5_out));
  LED led_10 (.in(and_5_out));
  LED led_11 (.in(and_5_out));
  LED led_12 (.in(and_5_out));
  LED led_13 (.in(not_2_out));
  LED led_14 (.in(not_2_out));
  LED led_15 (.in(not_2_out));
  LED led_16 (.in(not_2_out));
  LED led_17 (.in(not_2_out));
  LED led_18 (.in(not_2_out));
  LED led_19 (.in(not_2_out));
  LED led_20 (.in(not_2_out));
  LED led_21 (.in(and_6_out));
  LED led_22 (.in(and_6_out));
  LED led_23 (.in(and_6_out));
  LED led_24 (.in(and_6_out));
  LED led_25 (.in(and_6_out));
  LED led_26 (.in(and_6_out));
  LED led_27 (.in(not_2_out));
  LED led_28 (.in(not_2_out));

  // Notes on the sheet:
  //   Ayushi Gupta & Annabelle Crescenzo
  //   I pledge my honor that I have abided by the Stevens Honor System
  //   Core i382
  //   Destination Register
  //   Operation
endmodule

module nums (
  input  in_1,
  input  in_2,
  input  B,
  input  in_4,
  output a,
  output out_6,
  output c,
  output d,
  output e,
  output f,
  output g
);

  wire and_1_out, and_2_out, and_3_out, and_4_out, and_5_out, and_6_out, and_7_out, and_8_out, and_9_out,
       and_10_out, and_11_out, and_12_out, and_13_out, and_14_out, and_15_out, and_16_out, not_1_out,
       not_2_out, not_3_out;

  not not_1 (not_1_out, in_2);
  not not_2 (not_2_out, B);
  not not_3 (not_3_out, in_4);
  and and_1 (and_1_out, not_1_out, not_3_out);
  and and_2 (and_2_out, in_2, in_4);
  and and_3 (and_3_out, not_2_out, not_3_out);
  and and_4 (and_4_out, B, in_4);
  or or_1 (c, not_2_out, in_4, in_2);
  and and_5 (and_5_out, not_1_out, not_3_out);
  and and_6 (and_6_out, not_1_out, B);
  and and_7 (and_7_out, in_2, not_2_out, in_4);
  and and_8 (and_8_out, B, not_3_out);
  and and_9 (and_9_out, not_1_out, not_3_out);
  and and_10 (and_10_out, B, not_3_out);
  and and_11 (and_11_out, not_2_out, not_3_out);
  and and_12 (and_12_out, in_2, not_2_out);
  and and_13 (and_13_out, in_2, not_3_out);
  and and_14 (and_14_out, not_1_out, B);
  and and_15 (and_15_out, in_2, not_2_out);
  and and_16 (and_16_out, B, not_3_out);
  or or_2 (a, and_1_out, B, and_2_out, in_1);
  or or_3 (out_6, not_1_out, and_3_out, and_4_out);
  or or_4 (d, and_5_out, and_6_out, and_7_out, and_8_out, in_1);
  or or_5 (e, and_9_out, and_10_out);
  or or_6 (f, and_11_out, and_12_out, and_13_out, in_1);
  or or_7 (g, and_14_out, and_15_out, in_1, and_16_out);

  // Notes on the sheet:
  //   Combinational Logic for LED light
endmodule
